# Fritzing sketch Hobart H600 Timer (saved by Fritzing 0.9.9b)
circuit board: 7.14cm x 7.14022cm
breadboards: 1

parts:
  IRM-03-12 = MW-IRM-03-12
  J1 = 236-403 [part_number=236-403 package=THT]
  Arduino_Nano = Arduino NANO RP2040 CONNECT with headers
  Relay1 = RCI314012 [part_number=RCI314012 package=THT]
  J2 = 236-403 [part_number=236-403 package=THT]  # not connected
  Q1 = NPN-Transistor [part_number=BC817-40 package="SOT-23 [SMD]"]
  D1 = Schottky Diode [part_number=1N4148 package="Melf DO-213 AB [SMD]"]
  R1 = Resistor [tolerance=±5% resistance=1k power=0.25 package="0603 [SMD]"]
  J3 = female pin header, 3 pins [form="♀ (female)"]
  J4 = female pin header, 4 pins [form="♀ (female)"]
  J5 = screw terminal, 2 pins
  R2 = Resistor [tolerance=±5% resistance=10k package="0603 [SMD]"]
  J6 = female pin header, 2 pins [form="♀ (female)"]

nets (from the pcb view):
  N1: IRM-03-12.AC/L, J1.4
  N2: IRM-03-12.AC/N, J1.6
  N3: IRM-03-12.-Vo, Arduino_Nano.GND-4, Arduino_Nano.GND-29, Q1.2, J3.pin3, J4.pin4, R2.Pin_0
  N4: IRM-03-12.+Vo, Arduino_Nano.VIN, Relay1.A2, D1.cathode
  N5: Arduino_Nano.TX, J6.pin2
  N6: Arduino_Nano.RX, J6.pin1
  N7: Arduino_Nano.D2, J3.pin2
  N8: Arduino_Nano.D3, J3.pin1
  N9: Arduino_Nano.D4, J5.pin2, R2.Pin_1
  N10: Arduino_Nano.D17, R1.Pin_1
  N11: Arduino_Nano.D18, J4.pin1
  N12: Arduino_Nano.D19, J4.pin2
  N13: Arduino_Nano.+5V, J4.pin3, J5.pin1
  N14: Relay1.A1, Q1.1, D1.anode
  N15: Q1.0, R1.Pin_0

notes:
  L
  N
  11
  12
  14

custom parts:
  MW-IRM-03-12: AC-DC 220V to 12V Step-Down Power Supply Module
  236-403: WAGO PCB terminal block 236-403
  Arduino NANO RP2040 CONNECT with headers: Meet the only connected RP2040 board. It fits the Arduino Nano form factor, making it a small board with BIG features. The brain of the board is the Raspberry Pi RP2040 silicon; a dual-core Arm Cortex M0+ running at 133MHz. It has 264KB of SRAM, and the 16MB of flash memory is off-chip to give you extra storage. But what’s really exciting is the on-board connectivity options. The hugely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
  RCI314012: Weidmueller Relay RCI314012
